# Fritzing sketch wiring (saved by Fritzing 0.9.3b)
breadboards: 2

parts:
  Q1 = NPN-Transistor [package="TO92 [THT]"]
  Q2 = NPN-Transistor [package="TO92 [THT]"]
  Q3 = NPN-Transistor [package="TO92 [THT]"]
  Q4 = NPN-Transistor [package="TO92 [THT]"]
  Q5 = NPN-Transistor [package="TO92 [THT]"]
  Q6 = NPN-Transistor [package="TO92 [THT]"]
  R1 = Resistor [tolerance=±5% resistance=560 package=THT]
  R2 = Resistor [tolerance=±5% resistance=560 package=THT]
  R3 = Resistor [tolerance=±5% resistance=560 package=THT]
  R4 = Resistor [tolerance=±5% resistance=560 package=THT]
  R5 = Resistor [tolerance=±5% resistance=560 package=THT]
  R6 = Resistor [tolerance=±5% resistance=560 package=THT]
  Raspberry_Pi_Zero1 = Raspberry Pi Zero
  7_Segment2 = 7 Segment Display
  7_Segment3 = 7 Segment Display
  7_Segment4 = 7 Segment Display
  7_Segment5 = 7 Segment Display
  7_Segment6 = 7 Segment Display
  7_Segment7 = 7 Segment Display
  R7 = Resistor [tolerance=±5% resistance=200 package=THT]
  R8 = Resistor [tolerance=±5% resistance=200 package=THT]
  R9 = Resistor [tolerance=±5% resistance=200 package=THT]
  R10 = Resistor [tolerance=±5% resistance=200 package=THT]
  R11 = Resistor [tolerance=±5% resistance=200 package=THT]
  R12 = Resistor [tolerance=±5% resistance=200 package=THT]
  R13 = Resistor [tolerance=±5% resistance=200 package=THT]
  R14 = Resistor [tolerance=±5% resistance=200 package=THT]

nets:
  N1: Q1.E, Q2.E, Q3.E, Q4.E, Q5.E, Q6.E, Raspberry_Pi_Zero1.GND
  N2: Q1.B, R1.Pin_0
  N3: Q1.C, 7_Segment2.common_cathode
  N4: Q2.B, R2.Pin_0
  N5: Q2.C, 7_Segment3.common_cathode
  N6: Q3.B, R3.Pin_0
  N7: Q3.C, 7_Segment4.common_cathode
  N8: Q4.B, R4.Pin_0
  N9: Q4.C, 7_Segment6.common_cathode
  N10: Q5.B, R5.Pin_0
  N11: Q5.C, 7_Segment7.common_cathode
  N12: Q6.B, R6.Pin_0
  N13: Q6.C, 7_Segment5.common_cathode
  N14: R1.Pin_1, Raspberry_Pi_Zero1.GPIO22
  N15: R2.Pin_1, Raspberry_Pi_Zero1.GPIO5
  N16: R3.Pin_1, Raspberry_Pi_Zero1.GPIO6
  N17: R4.Pin_1, Raspberry_Pi_Zero1.GPIO13
  N18: R5.Pin_1, Raspberry_Pi_Zero1.GPIO19
  N19: R6.Pin_1, Raspberry_Pi_Zero1.GPIO26
  N20: Raspberry_Pi_Zero1.GPIO20, R14.Pin_1
  N21: Raspberry_Pi_Zero1.GPIO16, R13.Pin_1
  N22: Raspberry_Pi_Zero1.GPIO12, R12.Pin_1
  N23: Raspberry_Pi_Zero1.GPIO8, R11.Pin_1
  N24: Raspberry_Pi_Zero1.GPIO25, R10.Pin_1
  N25: Raspberry_Pi_Zero1.GPIO24, R9.Pin_1
  N26: Raspberry_Pi_Zero1.GPIO23, R8.Pin_1
  N27: Raspberry_Pi_Zero1.GPIO18, R7.Pin_1
  N28: 7_Segment2.Segment_E, 7_Segment3.Segment_E, 7_Segment4.Segment_E, 7_Segment5.Segment_E, 7_Segment6.Segment_E, 7_Segment7.Segment_E, R11.Pin_0
  N29: 7_Segment2.Segment_D, 7_Segment3.Segment_D, 7_Segment4.Segment_D, 7_Segment5.Segment_D, 7_Segment6.Segment_D, 7_Segment7.Segment_D, R10.Pin_0
  N30: 7_Segment2.Segment_C, 7_Segment3.Segment_C, 7_Segment4.Segment_C, 7_Segment5.Segment_C, 7_Segment6.Segment_C, 7_Segment7.Segment_C, R9.Pin_0
  N31: 7_Segment2.Segment_DP, 7_Segment3.Segment_DP, 7_Segment4.Segment_DP, 7_Segment5.Segment_DP, 7_Segment6.Segment_DP, 7_Segment7.Segment_DP, R14.Pin_0
  N32: 7_Segment2.Segment_B, 7_Segment4.Segment_B, 7_Segment5.Segment_B, 7_Segment6.Segment_B, 7_Segment7.Segment_B, R8.Pin_0
  N33: 7_Segment2.Segment_A, 7_Segment3.Segment_A, 7_Segment4.Segment_A, 7_Segment5.Segment_A, 7_Segment6.Segment_A, 7_Segment7.Segment_A, R7.Pin_0
  N34: 7_Segment2.Segment_F, 7_Segment3.Segment_F, 7_Segment4.Segment_F, 7_Segment5.Segment_F, 7_Segment6.Segment_F, 7_Segment7.Segment_F, R12.Pin_0
  N35: 7_Segment2.Segment_G, 7_Segment3.Segment_G, 7_Segment4.Segment_G, 7_Segment5.Segment_G, 7_Segment6.Segment_G, 7_Segment7.Segment_G, R13.Pin_0
